// Logisim project regfile.circ as structural Verilog: 1 circuit, main circuit regfile
module regfile (
  input  [4:0] rs1,
  input  [4:0] rs2,
  input  [4:0] rd,
  input  [31:0] Write_Data,
  input  RegWEn,
  input  clk,
  output [31:0] ra,
  output [31:0] sp,
  output [31:0] t0,
  output [31:0] t1,
  output [31:0] t2,
  output [31:0] s0,
  output [31:0] s1,
  output [31:0] a0,
  output [31:0] Read_Data_1,
  output [31:0] Read_Data_2
);

  wire clock_1_out, clock_2_out, clock_3_out, clock_4_out, clock_5_out, clock_6_out, clock_7_out,
       clock_8_out, clock_9_out, clock_10_out, clock_11_out, clock_12_out, clock_13_out, clock_14_out,
       clock_15_out, clock_16_out, clock_17_out, clock_18_out, clock_19_out, clock_20_out, clock_21_out,
       clock_22_out, clock_23_out, clock_24_out, clock_25_out, clock_26_out, clock_27_out, clock_28_out,
       clock_29_out, clock_30_out, clock_31_out, x1_write, x2_write, x3_write, x4_write, x5_write, x6_write,
       x7_write, x8_write, x9_write, x10_write, x11_write, x12_write, x13_write, x14_write, x15_write,
       x16_write, x17_write, x18_write, x19_write, x20_write, x21_write, x22_write, x23_write, x24_write,
       x25_write, x26_write, x27_write, x28_write, x29_write, x30_write, x31_write;
  wire [31:0] a1, a2, a3, a4, a5, a6, a7, gp, s2, s3, s4, s5, s6, s7, s8, s9, s10, s11, t3, t4, t5, t6, tp;

  Multiplexer #(.enable("false"), .select(5), .width(32)) multiplexer_1 (
    .in0({32{1'b0}}), .in1(ra), .in2(sp), .in3(gp), .in4(tp), .in5(t0), .in6(t1), .in7(t2), .in8(s0),
    .in9(s1), .in10(a0), .in11(a1), .in12(a2), .in13(a3), .in14(a4), .in15(a5), .in16(a6), .in17(a7),
    .in18(s2), .in19(s3), .in20(s4), .in21(s5), .in22(s6), .in23(s7), .in24(s8), .in25(s9), .in26(s10),
    .in27(s11), .in28(t3), .in29(t4), .in30(t5), .in31(t6), .out(Read_Data_1), .sel(rs1));
  Multiplexer #(.enable("false"), .select(5), .width(32)) multiplexer_2 (
    .in0({32{1'b0}}), .in1(ra), .in2(sp), .in3(gp), .in4(tp), .in5(t0), .in6(t1), .in7(t2), .in8(s0),
    .in9(s1), .in10(a0), .in11(a1), .in12(a2), .in13(a3), .in14(a4), .in15(a5), .in16(a6), .in17(a7),
    .in18(s2), .in19(s3), .in20(s4), .in21(s5), .in22(s6), .in23(s7), .in24(s8), .in25(s9), .in26(s10),
    .in27(s11), .in28(t3), .in29(t4), .in30(t5), .in31(t6), .out(Read_Data_2), .sel(rs2));
  Demultiplexer #(.enable("false"), .select(5)) demultiplexer_1 (
    .out1(x1_write), .out2(x2_write), .out3(x3_write), .out4(x4_write), .out5(x5_write), .out6(x6_write),
    .out7(x7_write), .out8(x8_write), .out9(x9_write), .out10(x10_write), .out11(x11_write),
    .out12(x12_write), .out13(x13_write), .out14(x14_write), .out15(x15_write), .out16(x16_write),
    .out17(x17_write), .out18(x18_write), .out19(x19_write), .out20(x20_write), .out21(x21_write),
    .out22(x22_write), .out23(x23_write), .out24(x24_write), .out25(x25_write), .out26(x26_write),
    .out27(x27_write), .out28(x28_write), .out29(x29_write), .out30(x30_write), .out31(x31_write),
    .in(RegWEn), .sel(rd));  // open: out0
  Register #(.width(32)) x25 (.D(Write_Data), .en(x25_write), .clk(clock_1_out), .Q(s9));  // open: clr
  Clock clock_1 (.out(clock_1_out));
  Register #(.width(32)) x26 (.D(Write_Data), .en(x26_write), .clk(clock_2_out), .Q(s10));  // open: clr
  Clock clock_2 (.out(clock_2_out));
  Register #(.width(32)) x27 (.D(Write_Data), .en(x27_write), .clk(clock_3_out), .Q(s11));  // open: clr
  Clock clock_3 (.out(clock_3_out));
  Register #(.width(32)) x28 (.D(Write_Data), .en(x28_write), .clk(clock_4_out), .Q(t3));  // open: clr
  Clock clock_4 (.out(clock_4_out));
  Register #(.width(32)) x29 (.D(Write_Data), .en(x29_write), .clk(clock_5_out), .Q(t4));  // open: clr
  Clock clock_5 (.out(clock_5_out));
  Register #(.width(32)) x30 (.D(Write_Data), .en(x30_write), .clk(clock_6_out), .Q(t5));  // open: clr
  Clock clock_6 (.out(clock_6_out));
  Register #(.width(32)) x31 (.D(Write_Data), .en(x31_write), .clk(clock_7_out), .Q(t6));  // open: clr
  Clock clock_7 (.out(clock_7_out));
  Register #(.width(32)) x1 (.D(Write_Data), .en(x1_write), .clk(clock_8_out), .Q(ra));  // open: clr
  Clock clock_8 (.out(clock_8_out));
  Register #(.width(32)) x2 (.D(Write_Data), .en(x2_write), .clk(clock_9_out), .Q(sp));  // open: clr
  Clock clock_9 (.out(clock_9_out));
  Register #(.width(32)) x3 (.D(Write_Data), .en(x3_write), .clk(clock_10_out), .Q(gp));  // open: clr
  Clock clock_10 (.out(clock_10_out));
  Register #(.width(32)) x4 (.D(Write_Data), .en(x4_write), .clk(clock_11_out), .Q(tp));  // open: clr
  Clock clock_11 (.out(clock_11_out));
  Register #(.width(32)) x5 (.D(Write_Data), .en(x5_write), .clk(clock_12_out), .Q(t0));  // open: clr
  Clock clock_12 (.out(clock_12_out));
  Register #(.width(32)) x6 (.D(Write_Data), .en(x6_write), .clk(clock_13_out), .Q(t1));  // open: clr
  Clock clock_13 (.out(clock_13_out));
  Register #(.width(32)) x7 (.D(Write_Data), .en(x7_write), .clk(clock_14_out), .Q(t2));  // open: clr
  Clock clock_14 (.out(clock_14_out));
  Register #(.width(32)) x8 (.D(Write_Data), .en(x8_write), .clk(clock_15_out), .Q(s0));  // open: clr
  Clock clock_15 (.out(clock_15_out));
  Register #(.width(32)) x9 (.D(Write_Data), .en(x9_write), .clk(clock_16_out), .Q(s1));  // open: clr
  Clock clock_16 (.out(clock_16_out));
  Register #(.width(32)) x10 (.D(Write_Data), .en(x10_write), .clk(clock_17_out), .Q(a0));  // open: clr
  Clock clock_17 (.out(clock_17_out));
  Register #(.width(32)) x11 (.D(Write_Data), .en(x11_write), .clk(clock_18_out), .Q(a1));  // open: clr
  Clock clock_18 (.out(clock_18_out));
  Register #(.width(32)) x12 (.D(Write_Data), .en(x12_write), .clk(clock_19_out), .Q(a2));  // open: clr
  Clock clock_19 (.out(clock_19_out));
  Register #(.width(32)) x13 (.D(Write_Data), .en(x13_write), .clk(clock_20_out), .Q(a3));  // open: clr
  Clock clock_20 (.out(clock_20_out));
  Register #(.width(32)) x14 (.D(Write_Data), .en(x14_write), .clk(clock_21_out), .Q(a4));  // open: clr
  Clock clock_21 (.out(clock_21_out));
  Register #(.width(32)) x15 (.D(Write_Data), .en(x15_write), .clk(clock_22_out), .Q(a5));  // open: clr
  Clock clock_22 (.out(clock_22_out));
  Register #(.width(32)) x16 (.D(Write_Data), .en(x16_write), .clk(clock_23_out), .Q(a6));  // open: clr
  Clock clock_23 (.out(clock_23_out));
  Register #(.width(32)) x17 (.D(Write_Data), .en(x17_write), .clk(clock_24_out), .Q(a7));  // open: clr
  Clock clock_24 (.out(clock_24_out));
  Register #(.width(32)) x18 (.D(Write_Data), .en(x18_write), .clk(clock_25_out), .Q(s2));  // open: clr
  Clock clock_25 (.out(clock_25_out));
  Register #(.width(32)) x19 (.D(Write_Data), .en(x19_write), .clk(clock_26_out), .Q(s3));  // open: clr
  Clock clock_26 (.out(clock_26_out));
  Register #(.width(32)) x20 (.D(Write_Data), .en(x20_write), .clk(clock_27_out));  // open: Q, clr
  Clock clock_27 (.out(clock_27_out));
  Register #(.width(32)) x21 (.D(Write_Data), .en(x21_write), .clk(clock_28_out), .Q(s5));  // open: clr
  Clock clock_28 (.out(clock_28_out));
  Register #(.width(32)) x22 (.D(Write_Data), .en(x22_write), .clk(clock_29_out), .Q(s6));  // open: clr
  Clock clock_29 (.out(clock_29_out));
  Register #(.width(32)) x23 (.D(Write_Data), .en(x23_write), .clk(clock_30_out), .Q(s7));  // open: clr
  Clock clock_30 (.out(clock_30_out));
  Register #(.width(32)) x24 (.D(Write_Data), .en(x24_write), .clk(clock_31_out), .Q(s8));  // open: clr
  Clock clock_31 (.out(clock_31_out));

  // Other names for the same wires on the sheet: read_data1[31:0] = Read_Data_1; read_data2[31:0] = Read_Data_2;
  //   read_reg1[4:0] = rs1; read_reg2[4:0] = rs2; write_en = RegWEn; write_reg[4:0] = rd

  // Notes on the sheet:
  //   INPUTS to your circuit
  //   DON'T CHANGE THE LOCATIONS OF THE INPUTS AND OUTPUTS!
  //   These are DEBUG/TEST outputs from your circuit.
  //   OUTPUTS from your circuit
endmodule
